# Fritzing sketch LED_MQTT (saved by Fritzing 0.9.10b)
breadboards: 1

parts:
  Mod1 = Amica NodeMCU DEVKIT 1.0
  S1 = Pushbutton [package="[THT]"]
  R1 = Resistor [tolerance=±5% power=0.25 resistance=220 package=THT]
  LED1 = LED - 3mm [color="Red (633nm)" current=0.030 package="3 mm [THT]"]

nets:
  N1: Mod1.pin1, Mod1.pin_10, Mod1.pin_26
  N2: Mod1.pin2, Mod1.pin_9, Mod1.pin_25, Mod1.pin_29, S1.Pin_3, S1.Pin_4, LED1.cathode
  N3: Mod1.pin_11, R1.Pin_1
  N4: Mod1.pin_23, S1.Pin_1, S1.Pin_2
  N5: R1.Pin_0, LED1.anode

notes:
  Estrutra de dados JSON:
  Ligar Led
  {
  "led": 1
  }
  Desligar Led
  {
  "led": 2
  }
